# Fritzing sketch ESP32_Art385_Platform (saved by Fritzing 0.9.3b)
breadboards: 1

parts:
  Part2 = Adafruit HUZZAH32 ESP32 Feather [part_number="Adafruit #3405"]
  LED2 = RGB LED (com. cathode, rgb) [package="5 mm [THT]"]
  R1 = Resistor [tolerance=±1% resistance=430 package=THT]
  R2 = Resistor [tolerance=±1% resistance=430 package=THT]
  R3 = Resistor [tolerance=±1% resistance=470 package=THT]
  R4 = Photocell (LDR) [package=THT]
  R5 = Resistor [tolerance=±0.5% resistance=10k package="1206 [SMD]"]
  U1 = POT [package=alps_pot]

nets:
  N1: Part2.A1_DAC1, U1.S
  N2: Part2.A0_DAC2, R4.pin_1, R5.Pin_0
  N3: Part2.GND, LED2.common_cathode, U1.A
  N4: Part2.3.3V, R4.pin_0, U1.E
  N5: Part2.IO12_A11, R3.Pin_0
  N6: Part2.IO33_A9, R1.Pin_0
  N7: LED2.red_anode, R3.Pin_1
  N8: LED2.green_anode, R1.Pin_1
  N9: LED2.blue_anode, R2.Pin_1
