# Fritzing sketch ESP32_LDR_LED (saved by Fritzing 0.9.3b)
breadboards: 1

parts:
  R1 = Photocell (LDR) [package=THT]
  R2 = Resistor [tolerance=±0.5% resistance=10k package="1206 [SMD]"]
  Part2 = Adafruit HUZZAH32 ESP32 Feather [part_number="Adafruit #3405"]
  LED1 = LED - 5mm [color="Red (633nm)" package="5 mm [THT]"]
  R3 = Resistor [tolerance=±5% resistance=100 package=THT]

nets:
  N1: R1.pin_0, R2.Pin_1, Part2.3.3V
  N2: R1.pin_1, R2.Pin_0, Part2.A0_DAC2
  N3: Part2.GND, R3.Pin_1
  N4: Part2.IO12_A11, LED1.cathode
  N5: LED1.anode, R3.Pin_0
