# Fritzing sketch ESP32_LED (saved by Fritzing 0.9.3b)
breadboards: 1

parts:
  Part2 = Adafruit HUZZAH32 ESP32 Feather [part_number="Adafruit #3405"]
  LED1 = LED - 5mm [color="Red (633nm)" package="5 mm [THT]"]
  R3 = Resistor [tolerance=±5% resistance=220 package=THT]

nets:
  N1: Part2.GND, R3.Pin_1
  N2: Part2.IO13_A12, LED1.cathode
  N3: LED1.anode, R3.Pin_0
