# Fritzing sketch ESP32_LED_RGB_forJake (saved by Fritzing 0.9.3b)
breadboards: 1

parts:
  Part2 = Adafruit HUZZAH32 ESP32 Feather [part_number="Adafruit #3405"]
  LED2 = RGB LED (com. cathode, rgb) [package="5 mm [THT]"]
  R1 = Resistor [tolerance=±1% resistance=430 package=THT]
  R2 = Resistor [tolerance=±1% resistance=430 package=THT]
  R3 = Resistor [tolerance=±1% resistance=470 package=THT]
  R4 = Rotary Potentiometer (Small) [maximum_resistance=100kΩ package=THT]
  R5 = Photocell (LDR) [package=THT]
  R6 = Resistor [tolerance=±5% resistance=10k package=THT]

nets:
  N1: Part2.A1_DAC1, R4.wiper
  N2: Part2.A0_DAC2, R5.pin_1, R6.Pin_0
  N3: Part2.GND, LED2.common_cathode, R4.leg1, R6.Pin_1
  N4: Part2.3.3V, R4.leg2, R5.pin_0
  N5: Part2.IO12_A11, R3.Pin_0
  N6: Part2.IO27_A10, R1.Pin_0
  N7: Part2.IO33_A9, R2.Pin_0
  N8: LED2.red_anode, R3.Pin_1
  N9: LED2.green_anode, R1.Pin_1
  N10: LED2.blue_anode, R2.Pin_1
